// Logisim project CONTROL_UNIT.circ as structural Verilog: 14 circuits, main circuit CU_main
module main (
  input  [3:0] in_1,
  input  [3:0] in_2,
  input  [3:0] in_3,
  input  [3:0] in_4,
  input  [3:0] in_5,
  input  [3:0] in_6,
  input  [3:0] in_7,
  input  [3:0] in_8,
  output [3:0] out_9,
  output [3:0] out_10
);

  wire and_1_out, and_2_out, clock_1_out, cu_main_1_add_sub, cu_main_1_dr_read, cu_main_1_dr_write,
       cu_main_1_mux_a, cu_main_1_mux_b, cu_main_1_pc_inc, cu_main_1_reg_update, cu_main_1_regwrite;
  wire [3:0] alu_1_a_out, alu_real_1_a_out, and_3_out, d_ff_1_q, dataram_1_out_6, multiplexer_1_out,
       registerblock_1_r1, registerblock_1_r2;
  wire [3:1] instructionregister_1_out_3;
  wire [3:3] cu_main_1_use_r1, instructionregister_1_out_3_2;

  Clock clock_1 (.out(clock_1_out));
  and and_1 (and_1_out, clock_1_out, cu_main_1_pc_inc);
  D_Flip_Flop #(.trigger("falling")) d_ff_1 (
    .D(alu_1_a_out[0]), .clk(and_1_out), .Q(d_ff_1_q[0]));  // open: Qn, preset, reset
  D_Flip_Flop #(.trigger("falling")) d_ff_2 (
    .D(alu_1_a_out[1]), .clk(and_1_out), .Q(d_ff_1_q[1]));  // open: Qn, preset, reset
  D_Flip_Flop #(.trigger("falling")) d_ff_3 (
    .D(alu_1_a_out[2]), .clk(and_1_out), .Q(d_ff_1_q[2]));  // open: Qn, preset, reset
  D_Flip_Flop #(.trigger("falling")) d_ff_4 (
    .D(alu_1_a_out[3]), .clk(and_1_out), .Q(d_ff_1_q[3]));  // open: Qn, preset, reset
  InstructionRAM instructionram_1 (
    .Clk(clock_1_out), .Instruction0(in_1), .Instruction1(in_2), .Instruction2(in_3), .Instruction3(in_4),
    .Instruction4(in_5), .Instruction5(in_6), .Instruction6(in_7), .Instruction7(in_8),
    .AddrBit0(d_ff_1_q[0]), .AddrBit1(d_ff_1_q[1]), .AddrBit2(d_ff_1_q[2]), .out_13(out_10));
  and and_2 (and_2_out, cu_main_1_reg_update, clock_1_out);
  ALU alu_1 (
    .L_Input(d_ff_1_q), .R_Input(4'b0001), .CLK(and_1_out), .A_out(alu_1_a_out));  // open: Add_Sub, Zero, Negative, Overflow
  CU_main cu_main_1 (
    .CLK(clock_1_out), .IR_4bit({instructionregister_1_out_3, instructionregister_1_out_3_2[3]}),
    .MUX_A(cu_main_1_mux_a), .DR_Read(cu_main_1_dr_read), .RegWrite(cu_main_1_regwrite),
    .Use_R1(cu_main_1_use_r1[3]), .MUX_B(cu_main_1_mux_b), .Add_Sub(cu_main_1_add_sub),
    .PC_Inc(cu_main_1_pc_inc), .Reg_Update(cu_main_1_reg_update), .DR_Write(cu_main_1_dr_write));
  InstructionRegister instructionregister_1 (
    .Clk(and_2_out), .in_2(out_10), .out_3({instructionregister_1_out_3, instructionregister_1_out_3_2[3]}));
  assign and_3_out = {4{cu_main_1_use_r1[3]}} & registerblock_1_r1;  // AND_Gate and_3, 4 bits wide
  RegisterBlock registerblock_1 (
    .Clk(clock_1_out), .in_2(out_9), .Addr(instructionregister_1_out_3[1]), .WriteReg(cu_main_1_regwrite),
    .ReadReg2(instructionregister_1_out_3_2[3]), .ReadReg1(instructionregister_1_out_3[1]),
    .R1(registerblock_1_r1), .R2(registerblock_1_r2));
  Multiplexer #(.width(4)) multiplexer_1 (
    .in0(registerblock_1_r2), .in1({4{instructionregister_1_out_3_2[3]}}), .out(multiplexer_1_out),
    .sel(cu_main_1_mux_a));
  ALU_REAL alu_real_1 (
    .L_input(and_3_out), .R_input(multiplexer_1_out), .CLK(clock_1_out), .Add_Sub(cu_main_1_add_sub),
    .A_out(alu_real_1_a_out));  // open: Zero, Negative, Overflow
  DataRAM dataram_1 (
    .Clk(clock_1_out), .in_2(registerblock_1_r1), .Addr(alu_real_1_a_out[3]), .Write(cu_main_1_dr_write),
    .Read(cu_main_1_dr_read), .out_6(dataram_1_out_6));
  Multiplexer #(.width(4)) multiplexer_2 (
    .in0(dataram_1_out_6), .in1(alu_real_1_a_out), .out(out_9), .sel(cu_main_1_mux_b));
endmodule

module CU_main (
  input  CLK,
  input  [3:0] IR_4bit,
  output MUX_A,
  output DR_Read,
  output RegWrite,
  output Use_R1,
  output MUX_B,
  output Add_Sub,
  output PC_Inc,
  output Reg_Update,
  output DR_Write
);

  wire and_1_out, and_2_out, and_3_out, and_4_out, and_5_out, and_7_out, and_8_out, and_9_out, and_11_out,
       and_15_out, and_16_out, and_17_out, and_20_out, and_21_out, decoder_1_out0, decoder_1_out1,
       decoder_1_out2, decoder_1_out3, decoder_2_out0, decoder_2_out1, decoder_2_out2, decoder_2_out3,
       not_1_out, PC_Inc1, PC_Inc2, PC_Inc3, PC_Inc4, Reg_Update4;
  wire [1:0] d_ff_1_q;
  wire [3:0] alu_1_a_out;

  D_Flip_Flop #(.trigger("falling")) d_ff_1 (
    .D(alu_1_a_out[0]), .clk(CLK), .Q(d_ff_1_q[0]));  // open: Qn, preset, reset
  D_Flip_Flop #(.trigger("falling")) d_ff_2 (
    .D(alu_1_a_out[1]), .clk(CLK), .Q(d_ff_1_q[1]));  // open: Qn, preset, reset
  Decoder #(.select(2)) decoder_1 (
    .out0(decoder_1_out0), .out1(decoder_1_out1), .out2(decoder_1_out2), .out3(decoder_1_out3), .sel(d_ff_1_q));  // open: en
  and and_1 (and_1_out, IR_4bit[0], IR_4bit[1], IR_4bit[3], IR_4bit[2]);
  not not_1 (not_1_out, and_1_out);
  Decoder #(.select(2)) decoder_2 (
    .out0(decoder_2_out0), .out1(decoder_2_out1), .out2(decoder_2_out2), .out3(decoder_2_out3),
    .sel(IR_4bit[3:2]), .en(not_1_out));
  and and_2 (and_2_out, decoder_2_out0, CLK);
  and and_3 (and_3_out, decoder_2_out1, CLK);
  and and_4 (and_4_out, decoder_2_out2, CLK);
  and and_5 (and_5_out, decoder_2_out3, CLK);
  ALU alu_1 (
    .L_Input({2'b00, d_ff_1_q}), .R_Input(4'b0001), .CLK(CLK), .A_out(alu_1_a_out));  // open: Add_Sub, Zero, Negative, Overflow
  and and_6 (PC_Inc1, decoder_1_out0, and_2_out);
  and and_7 (and_7_out, decoder_1_out1, and_2_out);
  and and_8 (and_8_out, decoder_1_out2, and_2_out);
  and and_9 (and_9_out, decoder_1_out3, and_2_out);
  and and_10 (PC_Inc2, decoder_1_out0, and_3_out);
  and and_11 (and_11_out, decoder_1_out1, and_3_out);
  and and_12 (DR_Write, decoder_1_out2, and_3_out);
  // AND_Gate and_13 has open pins: in0=decoder_1_out3, in1=and_3_out, out=open
  and and_14 (PC_Inc3, decoder_1_out0, and_4_out);
  and and_15 (and_15_out, decoder_1_out1, and_4_out);
  and and_16 (and_16_out, decoder_1_out2, and_4_out);
  and and_17 (and_17_out, decoder_1_out3, and_4_out);
  and and_18 (PC_Inc3, decoder_1_out0, and_5_out);
  and and_19 (Add_Sub, decoder_1_out1, and_5_out);
  and and_20 (and_20_out, decoder_1_out2, and_5_out);
  and and_21 (and_21_out, decoder_1_out3, and_5_out);
  or or_1 (MUX_A, and_7_out, and_11_out);
  buf or_2 (DR_Read, and_8_out);  // OR_Gate
  or or_3 (RegWrite, and_8_out, and_16_out, and_20_out);
  or or_4 (Use_R1, and_15_out, Add_Sub);
  or or_5 (MUX_B, and_16_out, and_20_out);
  or or_6 (PC_Inc, PC_Inc1, PC_Inc2, PC_Inc3, PC_Inc4);
  or or_7 (Reg_Update, PC_Inc1, PC_Inc2, PC_Inc3, Reg_Update4);

  // Other names for the same wires on the sheet: R2 = IR_4bit[0]; R1 = IR_4bit[1]; Reg_Update1 = PC_Inc1;
  //   Reg_Update2 = PC_Inc2; Reg_Update3 = PC_Inc3

  // Notes on the sheet:
  //   Step Counter
  //   op code
  //   Step
  //   R1
  //   R2 / ram 
  //   Load
  //   Save
  //   Add
  //   Syb
endmodule

module mainA (
  input  [3:0] in_1,
  input  in_2,
  input  in_3
);

  wire and_1_out, clock_1_out, cu_main_1_add_sub, cu_main_1_dr_read, cu_main_1_mux_a, cu_main_1_mux_b,
       cu_main_1_pc_inc, cu_main_1_reg_update, cu_main_1_regwrite, cu_main_1_use_r1;
  wire [2:0] d_ff_9_q;
  wire [3:0] alu_1_a_out, and_2_out, and_3_out, and_4_out, and_5_out, and_6_out, and_7_out, and_8_out,
       and_9_out, d_ff_1_q, d_ff_2_q, d_ff_3_q, d_ff_4_q, d_ff_5_q, d_ff_6_q, d_ff_7_q, d_ff_8_q, or_1_out;
  wire [3:3] d_ff_12_q, decoder_1_out0, decoder_1_out1, decoder_1_out2, decoder_1_out3, decoder_1_out4,
       decoder_1_out5, decoder_1_out6, decoder_1_out7;

  Clock clock_1 (.out(clock_1_out));
  Decoder #(.select(3)) decoder_1 (
    .out0(decoder_1_out0[3]), .out1(decoder_1_out1[3]), .out2(decoder_1_out2[3]), .out3(decoder_1_out3[3]),
    .out4(decoder_1_out4[3]), .out5(decoder_1_out5[3]), .out6(decoder_1_out6[3]), .out7(decoder_1_out7[3]),
    .sel(d_ff_9_q), .en(clock_1_out));
  and and_1 (and_1_out, clock_1_out, cu_main_1_pc_inc);
  D_Flip_Flop d_ff_1 (.Q(d_ff_1_q[0]));  // open: D, clk, Qn, preset, reset
  D_Flip_Flop d_ff_2 (.Q(d_ff_2_q[0]));  // open: D, clk, Qn, preset, reset
  D_Flip_Flop d_ff_3 (.Q(d_ff_3_q[0]));  // open: D, clk, Qn, preset, reset
  D_Flip_Flop d_ff_4 (.Q(d_ff_4_q[0]));  // open: D, clk, Qn, preset, reset
  D_Flip_Flop d_ff_5 (.Q(d_ff_5_q[0]));  // open: D, clk, Qn, preset, reset
  D_Flip_Flop d_ff_6 (.Q(d_ff_6_q[0]));  // open: D, clk, Qn, preset, reset
  D_Flip_Flop d_ff_7 (.Q(d_ff_7_q[0]));  // open: D, clk, Qn, preset, reset
  D_Flip_Flop d_ff_8 (.Q(d_ff_8_q[0]));  // open: D, clk, Qn, preset, reset
  D_Flip_Flop #(.trigger("falling")) d_ff_9 (
    .D(alu_1_a_out[0]), .clk(and_1_out), .Q(d_ff_9_q[0]));  // open: Qn, preset, reset
  D_Flip_Flop #(.trigger("falling")) d_ff_10 (
    .D(alu_1_a_out[1]), .clk(and_1_out), .Q(d_ff_9_q[1]));  // open: Qn, preset, reset
  D_Flip_Flop #(.trigger("falling")) d_ff_11 (
    .D(alu_1_a_out[2]), .clk(and_1_out), .Q(d_ff_9_q[2]));  // open: Qn, preset, reset
  D_Flip_Flop #(.trigger("falling")) d_ff_12 (
    .D(alu_1_a_out[3]), .clk(and_1_out), .Q(d_ff_12_q[3]));  // open: Qn, preset, reset
  D_Flip_Flop d_ff_13 (.Q(d_ff_1_q[1]));  // open: D, clk, Qn, preset, reset
  D_Flip_Flop d_ff_14 (.Q(d_ff_2_q[1]));  // open: D, clk, Qn, preset, reset
  D_Flip_Flop d_ff_15 (.Q(d_ff_3_q[1]));  // open: D, clk, Qn, preset, reset
  D_Flip_Flop d_ff_16 (.Q(d_ff_4_q[1]));  // open: D, clk, Qn, preset, reset
  D_Flip_Flop d_ff_17 (.Q(d_ff_5_q[1]));  // open: D, clk, Qn, preset, reset
  D_Flip_Flop d_ff_18 (.Q(d_ff_6_q[1]));  // open: D, clk, Qn, preset, reset
  D_Flip_Flop d_ff_19 (.Q(d_ff_7_q[1]));  // open: D, clk, Qn, preset, reset
  D_Flip_Flop d_ff_20 (.Q(d_ff_8_q[1]));  // open: D, clk, Qn, preset, reset
  CU_main cu_main_1 (
    .CLK(clock_1_out), .IR_4bit(or_1_out), .MUX_A(cu_main_1_mux_a), .DR_Read(cu_main_1_dr_read),
    .RegWrite(cu_main_1_regwrite), .Use_R1(cu_main_1_use_r1), .MUX_B(cu_main_1_mux_b),
    .Add_Sub(cu_main_1_add_sub), .PC_Inc(cu_main_1_pc_inc), .Reg_Update(cu_main_1_reg_update));  // open: DR_Write
  D_Flip_Flop d_ff_21 (.Q(d_ff_1_q[2]));  // open: D, clk, Qn, preset, reset
  D_Flip_Flop d_ff_22 (.Q(d_ff_2_q[2]));  // open: D, clk, Qn, preset, reset
  D_Flip_Flop d_ff_23 (.Q(d_ff_3_q[2]));  // open: D, clk, Qn, preset, reset
  D_Flip_Flop d_ff_24 (.Q(d_ff_4_q[2]));  // open: D, clk, Qn, preset, reset
  D_Flip_Flop d_ff_25 (.Q(d_ff_5_q[2]));  // open: D, clk, Qn, preset, reset
  D_Flip_Flop d_ff_26 (.Q(d_ff_6_q[2]));  // open: D, clk, Qn, preset, reset
  D_Flip_Flop d_ff_27 (.Q(d_ff_7_q[2]));  // open: D, clk, Qn, preset, reset
  D_Flip_Flop d_ff_28 (.Q(d_ff_8_q[2]));  // open: D, clk, Qn, preset, reset
  ALU alu_1 (
    .L_Input({d_ff_12_q[3], d_ff_9_q}), .R_Input(4'b0001), .CLK(and_1_out), .A_out(alu_1_a_out));  // open: Add_Sub, Zero, Negative, Overflow
  D_Flip_Flop d_ff_29 (.Q(d_ff_1_q[3]));  // open: D, clk, Qn, preset, reset
  D_Flip_Flop d_ff_30 (.Q(d_ff_2_q[3]));  // open: D, clk, Qn, preset, reset
  D_Flip_Flop d_ff_31 (.Q(d_ff_3_q[3]));  // open: D, clk, Qn, preset, reset
  D_Flip_Flop d_ff_32 (.Q(d_ff_4_q[3]));  // open: D, clk, Qn, preset, reset
  D_Flip_Flop d_ff_33 (.Q(d_ff_5_q[3]));  // open: D, clk, Qn, preset, reset
  D_Flip_Flop d_ff_34 (.Q(d_ff_6_q[3]));  // open: D, clk, Qn, preset, reset
  D_Flip_Flop d_ff_35 (.Q(d_ff_7_q[3]));  // open: D, clk, Qn, preset, reset
  D_Flip_Flop d_ff_36 (.Q(d_ff_8_q[3]));  // open: D, clk, Qn, preset, reset
  assign and_2_out = d_ff_1_q & {4{decoder_1_out0[3]}};  // AND_Gate and_2, 4 bits wide
  assign and_3_out = d_ff_2_q & {4{decoder_1_out1[3]}};  // AND_Gate and_3, 4 bits wide
  assign and_4_out = d_ff_3_q & {4{decoder_1_out2[3]}};  // AND_Gate and_4, 4 bits wide
  assign and_5_out = d_ff_4_q & {4{decoder_1_out3[3]}};  // AND_Gate and_5, 4 bits wide
  assign and_6_out = d_ff_5_q & {4{decoder_1_out4[3]}};  // AND_Gate and_6, 4 bits wide
  assign and_7_out = d_ff_6_q & {4{decoder_1_out5[3]}};  // AND_Gate and_7, 4 bits wide
  assign and_8_out = d_ff_7_q & {4{decoder_1_out6[3]}};  // AND_Gate and_8, 4 bits wide
  assign and_9_out = d_ff_8_q & {4{decoder_1_out7[3]}};  // AND_Gate and_9, 4 bits wide
  assign {or_1_out[0], or_1_out[1], or_1_out[2], or_1_out[3]} = and_2_out | and_3_out | and_4_out | and_5_out | and_6_out | and_7_out | and_8_out | and_9_out;  // OR_Gate or_1, 4 bits wide
  D_Flip_Flop #(.trigger("low")) d_ff_37 (.D(in_2), .clk(in_3));  // open: Q, Qn, preset, reset

  // Notes on the sheet:
  //   <---- IR Ram Test
endmodule

module ALU (
  input  [3:0] L_Input,
  input  [3:0] R_Input,
  input  CLK,
  input  Add_Sub,
  output Zero,
  output Negative,
  output Overflow,
  output [3:0] A_out
);

  wire and_1_out, and_2_out, and_3_out, and_4_out, and_5_out, and_6_out, and_7_out, and_8_out, and_9_out,
       and_10_out, and_11_out, and_12_out, and_13_out, and_14_out, and_15_out, and_16_out, and_17_out,
       and_18_out, and_19_out, and_20_out, and_21_out, and_22_out, and_24_out, and_25_out, and_26_out,
       and_27_out, fulladder_1_c, fulladder_2_c, fulladder_3_c, Neg_out, not_1_out, not_2_out, not_3_out,
       not_4_out, not_5_out, not_6_out, not_7_out, not_8_out, not_9_out, not_10_out, not_11_out, not_12_out,
       not_13_out, not_14_out, not_15_out, or_1_out, or_2_out, or_3_out, or_4_out, or_5_out, Pos_out,
       xor_2_out, xor_3_out, xor_4_out, xor_5_out;

  not not_1 (not_1_out, Add_Sub);
  and and_1 (and_1_out, L_Input[3], CLK);
  and and_2 (and_2_out, L_Input[2], CLK);
  and and_3 (and_3_out, L_Input[1], CLK);
  FullAdder fulladder_1 (.A(or_1_out), .B(and_1_out), .Carry(fulladder_2_c), .C(fulladder_1_c), .Sum(A_out[3]));
  and and_4 (and_4_out, L_Input[0], CLK);
  FullAdder fulladder_2 (.A(or_2_out), .B(and_2_out), .Carry(fulladder_3_c), .C(fulladder_2_c), .Sum(A_out[2]));
  or or_1 (or_1_out, xor_2_out, and_6_out);
  FullAdder fulladder_3 (.A(or_3_out), .B(and_3_out), .Carry(and_5_out), .C(fulladder_3_c), .Sum(A_out[1]));
  or or_2 (or_2_out, xor_3_out, and_8_out);
  or or_3 (or_3_out, xor_4_out, and_9_out);
  and and_5 (and_5_out, and_4_out, or_4_out);
  xor xor_1 (A_out[0], and_4_out, or_4_out);
  and and_6 (and_6_out, and_12_out, not_1_out);
  and and_7 (and_7_out, not_6_out, and_10_out);
  or or_4 (or_4_out, xor_5_out, and_14_out);
  not not_2 (not_2_out, A_out[0]);
  not not_3 (not_3_out, A_out[1]);
  not not_4 (not_4_out, A_out[2]);
  not not_5 (not_5_out, A_out[3]);
  and and_8 (and_8_out, and_13_out, not_1_out);
  and and_9 (and_9_out, and_17_out, not_1_out);
  xor xor_2 (xor_2_out, not_6_out, and_10_out);
  and and_10 (and_10_out, not_10_out, and_16_out);
  and and_11 (and_11_out, not_2_out, not_3_out, not_4_out, not_5_out);
  and and_12 (and_12_out, R_Input[3], CLK);
  and and_13 (and_13_out, R_Input[2], CLK);
  and and_14 (and_14_out, and_18_out, not_1_out);
  and and_15 (and_15_out, and_12_out, Add_Sub);
  not not_6 (not_6_out, and_15_out);
  xor xor_3 (xor_3_out, not_10_out, and_16_out);
  and and_16 (and_16_out, not_11_out, and_22_out);
  not not_7 (not_7_out, or_1_out);
  not not_8 (not_8_out, and_1_out);
  not not_9 (not_9_out, or_1_out);
  and and_17 (and_17_out, R_Input[1], CLK);
  and and_18 (and_18_out, R_Input[0], CLK);
  and and_19 (and_19_out, and_13_out, Add_Sub);
  and and_20 (and_20_out, and_17_out, Add_Sub);
  and and_21 (and_21_out, and_18_out, Add_Sub);
  not not_10 (not_10_out, and_19_out);
  not not_11 (not_11_out, and_20_out);
  not not_12 (not_12_out, and_21_out);
  xor xor_4 (xor_4_out, not_11_out, and_22_out);
  and and_22 (and_22_out, not_12_out, 1'b1);
  and Neg (Neg_out, or_1_out, and_1_out);
  and Pos (Pos_out, not_7_out, not_8_out);
  and and_23 (Zero, and_11_out, CLK);
  xor xor_5 (xor_5_out, not_12_out, 1'b1);
  and and_24 (and_24_out, A_out[3], Neg_out);
  and and_25 (and_25_out, Pos_out, A_out[3]);
  and and_26 (and_26_out, not_13_out, not_9_out, fulladder_1_c);
  not not_13 (not_13_out, Add_Sub);
  not not_14 (not_14_out, fulladder_1_c);
  and and_27 (and_27_out, and_24_out, not_14_out);
  or or_5 (or_5_out, and_26_out, and_25_out, and_27_out);
  not not_15 (not_15_out, Zero);
  and notZero (Overflow, or_5_out, not_15_out);

  assign Negative = A_out[3];

  // Other names for the same wires on the sheet: CMD = Add_Sub

  // Notes on the sheet:
  //   Add/Sub command
  //   0 add, 1 sub
  //   B Input
  //   L input
  //   A-out output
  //   A Input
  //   Adder
  //   R Input
  //   2's Complement
  //   Status output
  //   -8 + -8 is underflow (not supported)
endmodule

module FullAdder (
  input  A,
  input  B,
  input  Carry,
  output C,
  output Sum
);

  wire and_1_out, and_2_out, xor_1_out;

  and and_1 (and_1_out, A, B);
  xor xor_1 (xor_1_out, A, B);
  and and_2 (and_2_out, xor_1_out, Carry);
  or or_1 (C, and_1_out, and_2_out);
  xor xor_2 (Sum, xor_1_out, Carry);
endmodule

module MainB (
  input  [3:0] in_1,
  input  [3:0] in_2,
  input  [3:0] in_3,
  input  [3:0] in_4,
  input  [3:0] in_5,
  input  [3:0] in_6,
  input  [3:0] in_7,
  input  [3:0] in_8,
  input  in_9,
  input  in_10,
  input  in_11
);

  wire clock_1_out;
  wire [3:0] instructionram_1_out_13;

  Clock clock_1 (.out(clock_1_out));
  InstructionRAM instructionram_1 (
    .Clk(clock_1_out), .Instruction0(in_1), .Instruction1(in_2), .Instruction2(in_3), .Instruction3(in_4),
    .Instruction4(in_5), .Instruction5(in_6), .Instruction6(in_7), .Instruction7(in_8), .AddrBit0(in_9),
    .AddrBit1(in_10), .AddrBit2(in_11), .out_13(instructionram_1_out_13));
  InstructionRegister instructionregister_1 (.Clk(clock_1_out), .in_2(instructionram_1_out_13));  // open: out_3
  RegisterBlock registerblock_1 ();  // open: Clk, in_2, Addr, WriteReg, ReadReg2, ReadReg1, R1, R2
  DataRAM dataram_1 ();  // open: Clk, in_2, Addr, Write, Read, out_6
endmodule

module ALU_REAL (
  input  [3:0] L_input,
  input  [3:0] R_input,
  input  CLK,
  input  Add_Sub,
  output Zero,
  output Negative,
  output Overflow,
  output [3:0] A_out
);

  wire [3:0] alu_1_a_out;

  ALU alu_1 (
    .L_Input(L_input), .R_Input(R_input), .CLK(CLK), .Add_Sub(Add_Sub), .Zero(Zero), .Negative(Negative),
    .Overflow(Overflow), .A_out(alu_1_a_out));
  D_Flip_Flop #(.trigger("falling")) d_ff_1 (.D(alu_1_a_out[0]), .clk(CLK), .Q(A_out[0]));  // open: Qn, preset, reset
  D_Flip_Flop #(.trigger("falling")) d_ff_2 (.D(alu_1_a_out[1]), .clk(CLK), .Q(A_out[1]));  // open: Qn, preset, reset
  D_Flip_Flop #(.trigger("falling")) d_ff_3 (.D(alu_1_a_out[2]), .clk(CLK), .Q(A_out[2]));  // open: Qn, preset, reset
  D_Flip_Flop #(.trigger("falling")) d_ff_4 (.D(alu_1_a_out[3]), .clk(CLK), .Q(A_out[3]));  // open: Qn, preset, reset
endmodule

module InstructionRAM (
  input  Clk,
  input  [3:0] Instruction0,
  input  [3:0] Instruction1,
  input  [3:0] Instruction2,
  input  [3:0] Instruction3,
  input  [3:0] Instruction4,
  input  [3:0] Instruction5,
  input  [3:0] Instruction6,
  input  [3:0] Instruction7,
  input  AddrBit0,
  input  AddrBit1,
  input  AddrBit2,
  output [3:0] out_13
);

  wire decoder_1_out0, decoder_1_out1, decoder_1_out2, decoder_1_out3, decoder_1_out4, decoder_1_out5,
       decoder_1_out6, decoder_1_out7, irnibble_1_out_7, irnibble_1_out_8, irnibble_1_out_9,
       irnibble_1_out_10, irnibble_2_out_7, irnibble_2_out_8, irnibble_2_out_9, irnibble_2_out_10,
       irnibble_3_out_7, irnibble_3_out_8, irnibble_3_out_9, irnibble_3_out_10, irnibble_4_out_7,
       irnibble_4_out_8, irnibble_4_out_9, irnibble_4_out_10, irnibble_5_out_7, irnibble_5_out_8,
       irnibble_5_out_9, irnibble_5_out_10, irnibble_6_out_7, irnibble_6_out_8, irnibble_6_out_9,
       irnibble_6_out_10, irnibble_7_out_7, irnibble_7_out_8, irnibble_7_out_9, irnibble_7_out_10,
       irnibble_8_out_7, irnibble_8_out_8, irnibble_8_out_9, irnibble_8_out_10, or_1_out, or_2_out, or_3_out,
       or_4_out, or_5_out, or_6_out, or_7_out, or_8_out, or_9_out, or_10_out, or_11_out, or_12_out,
       or_13_out, or_14_out, or_15_out, or_16_out, or_17_out, or_18_out, or_19_out, or_20_out, or_21_out,
       or_22_out, or_23_out, or_24_out, or_25_out, or_26_out, or_27_out, or_28_out;

  Decoder #(.select(3)) decoder_1 (
    .out0(decoder_1_out0), .out1(decoder_1_out1), .out2(decoder_1_out2), .out3(decoder_1_out3),
    .out4(decoder_1_out4), .out5(decoder_1_out5), .out6(decoder_1_out6), .out7(decoder_1_out7),
    .sel({AddrBit2, AddrBit1, AddrBit0}));  // open: en
  IRNibble irnibble_1 (
    .Bit0(Instruction0[3]), .Clk(Clk), .Bit1(Instruction0[2]), .Bit2(Instruction0[1]),
    .Bit3(Instruction0[0]), .Addr(decoder_1_out0), .out_7(irnibble_1_out_7), .out_8(irnibble_1_out_8),
    .out_9(irnibble_1_out_9), .out_10(irnibble_1_out_10));
  buf or_1 (or_1_out, irnibble_1_out_7);  // OR_Gate
  buf or_2 (or_2_out, irnibble_1_out_8);  // OR_Gate
  buf or_3 (or_3_out, irnibble_1_out_9);  // OR_Gate
  buf or_4 (or_4_out, irnibble_1_out_10);  // OR_Gate
  IRNibble irnibble_2 (
    .Bit0(Instruction1[3]), .Clk(Clk), .Bit1(Instruction1[2]), .Bit2(Instruction1[1]),
    .Bit3(Instruction1[0]), .Addr(decoder_1_out1), .out_7(irnibble_2_out_7), .out_8(irnibble_2_out_8),
    .out_9(irnibble_2_out_9), .out_10(irnibble_2_out_10));
  or or_5 (or_5_out, irnibble_2_out_7, or_1_out);
  or or_6 (or_6_out, irnibble_2_out_8, or_2_out);
  or or_7 (or_7_out, irnibble_2_out_9, or_3_out);
  or or_8 (or_8_out, irnibble_2_out_10, or_4_out);
  IRNibble irnibble_3 (
    .Bit0(Instruction2[3]), .Clk(Clk), .Bit1(Instruction2[2]), .Bit2(Instruction2[1]),
    .Bit3(Instruction2[0]), .Addr(decoder_1_out2), .out_7(irnibble_3_out_7), .out_8(irnibble_3_out_8),
    .out_9(irnibble_3_out_9), .out_10(irnibble_3_out_10));
  or or_9 (or_9_out, irnibble_3_out_7, or_5_out);
  or or_10 (or_10_out, irnibble_3_out_8, or_6_out);
  or or_11 (or_11_out, irnibble_3_out_9, or_7_out);
  or or_12 (or_12_out, irnibble_3_out_10, or_8_out);
  IRNibble irnibble_4 (
    .Bit0(Instruction3[3]), .Clk(Clk), .Bit1(Instruction3[2]), .Bit2(Instruction3[1]),
    .Bit3(Instruction3[0]), .Addr(decoder_1_out3), .out_7(irnibble_4_out_7), .out_8(irnibble_4_out_8),
    .out_9(irnibble_4_out_9), .out_10(irnibble_4_out_10));
  or or_13 (or_13_out, irnibble_4_out_7, or_9_out);
  or or_14 (or_14_out, irnibble_4_out_8, or_10_out);
  or or_15 (or_15_out, irnibble_4_out_9, or_11_out);
  or or_16 (or_16_out, irnibble_4_out_10, or_12_out);
  IRNibble irnibble_5 (
    .Bit0(Instruction4[3]), .Clk(Clk), .Bit1(Instruction4[2]), .Bit2(Instruction4[1]),
    .Bit3(Instruction4[0]), .Addr(decoder_1_out4), .out_7(irnibble_5_out_7), .out_8(irnibble_5_out_8),
    .out_9(irnibble_5_out_9), .out_10(irnibble_5_out_10));
  or or_17 (or_17_out, irnibble_5_out_7, or_13_out);
  or or_18 (or_18_out, irnibble_5_out_8, or_14_out);
  or or_19 (or_19_out, irnibble_5_out_9, or_15_out);
  or or_20 (or_20_out, irnibble_5_out_10, or_16_out);
  IRNibble irnibble_6 (
    .Bit0(Instruction5[3]), .Clk(Clk), .Bit1(Instruction5[2]), .Bit2(Instruction5[1]),
    .Bit3(Instruction5[0]), .Addr(decoder_1_out5), .out_7(irnibble_6_out_7), .out_8(irnibble_6_out_8),
    .out_9(irnibble_6_out_9), .out_10(irnibble_6_out_10));
  or or_21 (or_21_out, irnibble_6_out_7, or_17_out);
  or or_22 (or_22_out, irnibble_6_out_8, or_18_out);
  or or_23 (or_23_out, irnibble_6_out_9, or_19_out);
  or or_24 (or_24_out, irnibble_6_out_10, or_20_out);
  IRNibble irnibble_7 (
    .Bit0(Instruction6[3]), .Clk(Clk), .Bit1(Instruction6[2]), .Bit2(Instruction6[1]),
    .Bit3(Instruction6[0]), .Addr(decoder_1_out6), .out_7(irnibble_7_out_7), .out_8(irnibble_7_out_8),
    .out_9(irnibble_7_out_9), .out_10(irnibble_7_out_10));
  or or_25 (or_25_out, irnibble_7_out_7, or_21_out);
  or or_26 (or_26_out, irnibble_7_out_8, or_22_out);
  or or_27 (or_27_out, irnibble_7_out_9, or_23_out);
  or or_28 (or_28_out, irnibble_7_out_10, or_24_out);
  IRNibble irnibble_8 (
    .Bit0(Instruction7[3]), .Clk(Clk), .Bit1(Instruction7[2]), .Bit2(Instruction7[1]),
    .Bit3(Instruction7[0]), .Addr(decoder_1_out7), .out_7(irnibble_8_out_7), .out_8(irnibble_8_out_8),
    .out_9(irnibble_8_out_9), .out_10(irnibble_8_out_10));
  or or_29 (out_13[3], irnibble_8_out_7, or_25_out);
  or or_30 (out_13[2], irnibble_8_out_8, or_26_out);
  or or_31 (out_13[1], irnibble_8_out_9, or_27_out);
  or or_32 (out_13[0], irnibble_8_out_10, or_28_out);
endmodule

module InstructionRegister (
  input  Clk,
  input  [3:0] in_2,
  output [3:0] out_3
);

  wire not_1_out, not_2_out, not_3_out, not_4_out, not_5_out, not_6_out;

  not not_1 (not_1_out, Clk);
  not not_2 (not_2_out, not_1_out);
  not not_3 (not_3_out, not_2_out);
  not not_4 (not_4_out, not_3_out);
  not not_5 (not_5_out, not_4_out);
  not not_6 (not_6_out, not_5_out);
  Nibble nibble_1 (
    .Bit0(in_2[3]), .Clk(not_6_out), .Bit1(in_2[2]), .Bit2(in_2[1]), .Bit3(in_2[0]), .Addr(1'b1),
    .out_7(out_3[3]), .out_8(out_3[2]), .out_9(out_3[1]), .out_10(out_3[0]));
endmodule

module RegisterBlock (
  input  Clk,
  input  [3:0] in_2,
  input  Addr,
  input  WriteReg,
  input  ReadReg2,
  input  ReadReg1,
  output [3:0] R1,
  output [3:0] R2
);

  wire and_1_out, not_1_out;
  wire [3:0] rbnibble_1_out_10, rbnibble_2_out_10;

  and and_1 (and_1_out, Clk, WriteReg);
  not not_1 (not_1_out, Addr);
  RBNibble rbnibble_1 (
    .Bit0(in_2[3]), .Clk(and_1_out), .Bit1(in_2[2]), .Bit2(in_2[1]), .Bit3(in_2[0]), .Addr(not_1_out),
    .out_7(rbnibble_1_out_10[3]), .out_8(rbnibble_1_out_10[2]), .out_9(rbnibble_1_out_10[1]),
    .out_10(rbnibble_1_out_10[0]));
  RBNibble rbnibble_2 (
    .Bit0(in_2[3]), .Clk(and_1_out), .Bit1(in_2[2]), .Bit2(in_2[1]), .Bit3(in_2[0]), .Addr(Addr),
    .out_7(rbnibble_2_out_10[3]), .out_8(rbnibble_2_out_10[2]), .out_9(rbnibble_2_out_10[1]),
    .out_10(rbnibble_2_out_10[0]));
  Multiplexer #(.width(4)) multiplexer_1 (.in0(rbnibble_1_out_10), .in1(rbnibble_2_out_10), .out(R1), .sel(ReadReg1));
  Multiplexer #(.width(4)) multiplexer_2 (.in0(rbnibble_1_out_10), .in1(rbnibble_2_out_10), .out(R2), .sel(ReadReg2));
endmodule

module DataRAM (
  input  Clk,
  input  [3:0] in_2,
  input  Addr,
  input  Write,
  input  Read,
  output [3:0] out_6
);

  wire and_1_out, and_2_out, and_3_out, and_4_out, and_5_out, and_6_out, and_7_out, and_8_out, and_9_out,
       nibble_1_out_7, nibble_1_out_8, nibble_1_out_9, nibble_1_out_10, nibble_2_out_7, nibble_2_out_8,
       nibble_2_out_9, nibble_2_out_10, not_1_out;

  and and_1 (and_1_out, Clk, Write);
  not not_1 (not_1_out, Addr);
  Nibble nibble_1 (
    .Bit0(in_2[3]), .Clk(and_1_out), .Bit1(in_2[2]), .Bit2(in_2[1]), .Bit3(in_2[0]), .Addr(not_1_out),
    .out_7(nibble_1_out_7), .out_8(nibble_1_out_8), .out_9(nibble_1_out_9), .out_10(nibble_1_out_10));
  Nibble nibble_2 (
    .Bit0(in_2[3]), .Clk(and_1_out), .Bit1(in_2[2]), .Bit2(in_2[1]), .Bit3(in_2[0]), .Addr(Addr),
    .out_7(nibble_2_out_7), .out_8(nibble_2_out_8), .out_9(nibble_2_out_9), .out_10(nibble_2_out_10));
  and and_2 (and_2_out, nibble_1_out_7, Read);
  and and_3 (and_3_out, nibble_1_out_8, Read);
  and and_4 (and_4_out, nibble_1_out_9, Read);
  and and_5 (and_5_out, nibble_1_out_10, Read);
  and and_6 (and_6_out, nibble_2_out_7, Read);
  and and_7 (and_7_out, nibble_2_out_8, Read);
  and and_8 (and_8_out, nibble_2_out_9, Read);
  and and_9 (and_9_out, nibble_2_out_10, Read);
  or or_1 (out_6[3], and_2_out, and_6_out);
  or or_2 (out_6[2], and_3_out, and_7_out);
  or or_3 (out_6[1], and_4_out, and_8_out);
  or or_4 (out_6[0], and_5_out, and_9_out);
endmodule

module Nibble (
  input  Bit0,
  input  Clk,
  input  Bit1,
  input  Bit2,
  input  Bit3,
  input  Addr,
  output out_7,
  output out_8,
  output out_9,
  output out_10
);

  wire and_1_out, and_2_out, and_3_out, and_4_out, d_ff_1_q, d_ff_2_q, d_ff_3_q, d_ff_4_q;

  D_Flip_Flop #(.trigger("falling")) d_ff_1 (.D(Bit0), .clk(and_1_out), .Q(d_ff_1_q));  // open: Qn, preset, reset
  and and_1 (and_1_out, Addr, Clk);
  D_Flip_Flop #(.trigger("falling")) d_ff_2 (.D(Bit1), .clk(and_2_out), .Q(d_ff_2_q));  // open: Qn, preset, reset
  and and_2 (and_2_out, Addr, Clk);
  D_Flip_Flop #(.trigger("falling")) d_ff_3 (.D(Bit2), .clk(and_3_out), .Q(d_ff_3_q));  // open: Qn, preset, reset
  and and_3 (and_3_out, Addr, Clk);
  D_Flip_Flop #(.trigger("falling")) d_ff_4 (.D(Bit3), .clk(and_4_out), .Q(d_ff_4_q));  // open: Qn, preset, reset
  and and_4 (and_4_out, Addr, Clk);
  and and_5 (out_7, d_ff_1_q, Addr);
  and and_6 (out_8, d_ff_2_q, Addr);
  and and_7 (out_9, d_ff_3_q, Addr);
  and and_8 (out_10, d_ff_4_q, Addr);
endmodule

module IRNibble (
  input  Bit0,
  input  Clk,
  input  Bit1,
  input  Bit2,
  input  Bit3,
  input  Addr,
  output out_7,
  output out_8,
  output out_9,
  output out_10
);

  wire d_ff_1_q, d_ff_2_q, d_ff_3_q, d_ff_4_q;

  D_Flip_Flop #(.trigger("low")) d_ff_1 (.D(Bit0), .clk(1'b0), .Q(d_ff_1_q));  // open: Qn, preset, reset
  D_Flip_Flop #(.trigger("low")) d_ff_2 (.D(Bit1), .clk(1'b0), .Q(d_ff_2_q));  // open: Qn, preset, reset
  D_Flip_Flop #(.trigger("low")) d_ff_3 (.D(Bit2), .clk(1'b0), .Q(d_ff_3_q));  // open: Qn, preset, reset
  D_Flip_Flop #(.trigger("low")) d_ff_4 (.D(Bit3), .clk(1'b0), .Q(d_ff_4_q));  // open: Qn, preset, reset
  and and_1 (out_7, d_ff_1_q, Addr);
  and and_2 (out_8, d_ff_2_q, Addr);
  and and_3 (out_9, d_ff_3_q, Addr);
  and and_4 (out_10, d_ff_4_q, Addr);
endmodule

module RBNibble (
  input  Bit0,
  input  Clk,
  input  Bit1,
  input  Bit2,
  input  Bit3,
  input  Addr,
  output out_7,
  output out_8,
  output out_9,
  output out_10
);

  wire and_1_out, and_2_out, and_3_out, and_4_out, d_ff_1_q, d_ff_2_q, d_ff_3_q, d_ff_4_q;

  D_Flip_Flop #(.trigger("falling")) d_ff_1 (.D(Bit0), .clk(and_1_out), .Q(d_ff_1_q));  // open: Qn, preset, reset
  and and_1 (and_1_out, Addr, Clk);
  D_Flip_Flop #(.trigger("falling")) d_ff_2 (.D(Bit1), .clk(and_2_out), .Q(d_ff_2_q));  // open: Qn, preset, reset
  and and_2 (and_2_out, Addr, Clk);
  D_Flip_Flop #(.trigger("falling")) d_ff_3 (.D(Bit2), .clk(and_3_out), .Q(d_ff_3_q));  // open: Qn, preset, reset
  and and_3 (and_3_out, Addr, Clk);
  D_Flip_Flop #(.trigger("falling")) d_ff_4 (.D(Bit3), .clk(and_4_out), .Q(d_ff_4_q));  // open: Qn, preset, reset
  and and_4 (and_4_out, Addr, Clk);
  buf and_5 (out_7, d_ff_1_q);  // AND_Gate
  buf and_6 (out_8, d_ff_2_q);  // AND_Gate
  buf and_7 (out_9, d_ff_3_q);  // AND_Gate
  buf and_8 (out_10, d_ff_4_q);  // AND_Gate
endmodule
