// Logisim project MainB.circ as structural Verilog: 8 circuits, main circuit MainB
module MainB (
  input  [3:0] in_1,
  input  [3:0] in_2,
  input  [3:0] in_3,
  input  [3:0] in_4,
  input  [3:0] in_5,
  input  [3:0] in_6,
  input  [3:0] in_7,
  input  [3:0] in_8,
  input  in_9,
  input  in_10,
  input  in_11
);

  wire clock_1_out;
  wire [3:0] instructionram_1_out_13;

  Clock clock_1 (.out(clock_1_out));
  InstructionRAM instructionram_1 (
    .Clk(clock_1_out), .Instruction0(in_1), .Instruction1(in_2), .Instruction2(in_3), .Instruction3(in_4),
    .Instruction4(in_5), .Instruction5(in_6), .Instruction6(in_7), .Instruction7(in_8), .AddrBit0(in_9),
    .AddrBit1(in_10), .AddrBit2(in_11), .out_13(instructionram_1_out_13));
  InstructionRegister instructionregister_1 (.Clk(clock_1_out));  // open: in_2, out_3
  RegisterBlock registerblock_1 ();  // open: Clk, in_2, ReadReg1, Addr, WriteReg, ReadReg2, R1, R2
  DataRAM dataram_1 ();  // open: Clk, in_2, Addr, Mode, out_5
endmodule

module InstructionRAM (
  input  Clk,
  input  [3:0] Instruction0,
  input  [3:0] Instruction1,
  input  [3:0] Instruction2,
  input  [3:0] Instruction3,
  input  [3:0] Instruction4,
  input  [3:0] Instruction5,
  input  [3:0] Instruction6,
  input  [3:0] Instruction7,
  input  AddrBit0,
  input  AddrBit1,
  input  AddrBit2,
  output [3:0] out_13
);

  wire decoder_1_out0, decoder_1_out1, decoder_1_out2, decoder_1_out3, decoder_1_out4, decoder_1_out5,
       decoder_1_out6, decoder_1_out7, nibble_1_out_7, nibble_1_out_8, nibble_1_out_9, nibble_1_out_10,
       nibble_2_out_7, nibble_2_out_8, nibble_2_out_9, nibble_2_out_10, nibble_3_out_7, nibble_3_out_8,
       nibble_3_out_9, nibble_3_out_10, nibble_4_out_7, nibble_4_out_8, nibble_4_out_9, nibble_4_out_10,
       nibble_5_out_7, nibble_5_out_8, nibble_5_out_9, nibble_5_out_10, nibble_6_out_7, nibble_6_out_8,
       nibble_6_out_9, nibble_6_out_10, nibble_7_out_7, nibble_7_out_8, nibble_7_out_9, nibble_7_out_10,
       nibble_8_out_7, nibble_8_out_8, nibble_8_out_9, nibble_8_out_10, or_1_out, or_2_out, or_3_out,
       or_4_out, or_5_out, or_6_out, or_7_out, or_8_out, or_9_out, or_10_out, or_11_out, or_12_out,
       or_13_out, or_14_out, or_15_out, or_16_out, or_17_out, or_18_out, or_19_out, or_20_out, or_21_out,
       or_22_out, or_23_out, or_24_out, or_25_out, or_26_out, or_27_out, or_28_out;

  Decoder #(.select(3)) decoder_1 (
    .out0(decoder_1_out0), .out1(decoder_1_out1), .out2(decoder_1_out2), .out3(decoder_1_out3),
    .out4(decoder_1_out4), .out5(decoder_1_out5), .out6(decoder_1_out6), .out7(decoder_1_out7),
    .sel({AddrBit2, AddrBit1, AddrBit0}));  // open: en
  Nibble nibble_1 (
    .Bit0(Instruction0[3]), .Clk(Clk), .Bit1(Instruction0[2]), .Bit2(Instruction0[1]),
    .Bit3(Instruction0[0]), .Addr(decoder_1_out0), .out_7(nibble_1_out_7), .out_8(nibble_1_out_8),
    .out_9(nibble_1_out_9), .out_10(nibble_1_out_10));
  buf or_1 (or_1_out, nibble_1_out_7);  // OR_Gate
  buf or_2 (or_2_out, nibble_1_out_8);  // OR_Gate
  buf or_3 (or_3_out, nibble_1_out_9);  // OR_Gate
  buf or_4 (or_4_out, nibble_1_out_10);  // OR_Gate
  Nibble nibble_2 (
    .Bit0(Instruction1[3]), .Clk(Clk), .Bit1(Instruction1[2]), .Bit2(Instruction1[1]),
    .Bit3(Instruction1[0]), .Addr(decoder_1_out1), .out_7(nibble_2_out_7), .out_8(nibble_2_out_8),
    .out_9(nibble_2_out_9), .out_10(nibble_2_out_10));
  or or_5 (or_5_out, nibble_2_out_7, or_1_out);
  or or_6 (or_6_out, nibble_2_out_8, or_2_out);
  or or_7 (or_7_out, nibble_2_out_9, or_3_out);
  or or_8 (or_8_out, nibble_2_out_10, or_4_out);
  Nibble nibble_3 (
    .Bit0(Instruction2[3]), .Clk(Clk), .Bit1(Instruction2[2]), .Bit2(Instruction2[1]),
    .Bit3(Instruction2[0]), .Addr(decoder_1_out2), .out_7(nibble_3_out_7), .out_8(nibble_3_out_8),
    .out_9(nibble_3_out_9), .out_10(nibble_3_out_10));
  or or_9 (or_9_out, nibble_3_out_7, or_5_out);
  or or_10 (or_10_out, nibble_3_out_8, or_6_out);
  or or_11 (or_11_out, nibble_3_out_9, or_7_out);
  or or_12 (or_12_out, nibble_3_out_10, or_8_out);
  Nibble nibble_4 (
    .Bit0(Instruction3[3]), .Clk(Clk), .Bit1(Instruction3[2]), .Bit2(Instruction3[1]),
    .Bit3(Instruction3[0]), .Addr(decoder_1_out3), .out_7(nibble_4_out_7), .out_8(nibble_4_out_8),
    .out_9(nibble_4_out_9), .out_10(nibble_4_out_10));
  or or_13 (or_13_out, nibble_4_out_7, or_9_out);
  or or_14 (or_14_out, nibble_4_out_8, or_10_out);
  or or_15 (or_15_out, nibble_4_out_9, or_11_out);
  or or_16 (or_16_out, nibble_4_out_10, or_12_out);
  Nibble nibble_5 (
    .Bit0(Instruction4[3]), .Clk(Clk), .Bit1(Instruction4[2]), .Bit2(Instruction4[1]),
    .Bit3(Instruction4[0]), .Addr(decoder_1_out4), .out_7(nibble_5_out_7), .out_8(nibble_5_out_8),
    .out_9(nibble_5_out_9), .out_10(nibble_5_out_10));
  or or_17 (or_17_out, nibble_5_out_7, or_13_out);
  or or_18 (or_18_out, nibble_5_out_8, or_14_out);
  or or_19 (or_19_out, nibble_5_out_9, or_15_out);
  or or_20 (or_20_out, nibble_5_out_10, or_16_out);
  Nibble nibble_6 (
    .Bit0(Instruction5[3]), .Clk(Clk), .Bit1(Instruction5[2]), .Bit2(Instruction5[1]),
    .Bit3(Instruction5[0]), .Addr(decoder_1_out5), .out_7(nibble_6_out_7), .out_8(nibble_6_out_8),
    .out_9(nibble_6_out_9), .out_10(nibble_6_out_10));
  or or_21 (or_21_out, nibble_6_out_7, or_17_out);
  or or_22 (or_22_out, nibble_6_out_8, or_18_out);
  or or_23 (or_23_out, nibble_6_out_9, or_19_out);
  or or_24 (or_24_out, nibble_6_out_10, or_20_out);
  Nibble nibble_7 (
    .Bit0(Instruction6[3]), .Clk(Clk), .Bit1(Instruction6[2]), .Bit2(Instruction6[1]),
    .Bit3(Instruction6[0]), .Addr(decoder_1_out6), .out_7(nibble_7_out_7), .out_8(nibble_7_out_8),
    .out_9(nibble_7_out_9), .out_10(nibble_7_out_10));
  or or_25 (or_25_out, nibble_7_out_7, or_21_out);
  or or_26 (or_26_out, nibble_7_out_8, or_22_out);
  or or_27 (or_27_out, nibble_7_out_9, or_23_out);
  or or_28 (or_28_out, nibble_7_out_10, or_24_out);
  Nibble nibble_8 (
    .Bit0(Instruction7[3]), .Clk(Clk), .Bit1(Instruction7[2]), .Bit2(Instruction7[1]),
    .Bit3(Instruction7[0]), .Addr(decoder_1_out7), .out_7(nibble_8_out_7), .out_8(nibble_8_out_8),
    .out_9(nibble_8_out_9), .out_10(nibble_8_out_10));
  or or_29 (out_13[3], nibble_8_out_7, or_25_out);
  or or_30 (out_13[2], nibble_8_out_8, or_26_out);
  or or_31 (out_13[1], nibble_8_out_9, or_27_out);
  or or_32 (out_13[0], nibble_8_out_10, or_28_out);
endmodule

module InstructionRegister (
  input  Clk,
  input  [3:0] in_2,
  output [3:0] out_3
);

  Nibble nibble_1 (
    .Bit0(in_2[3]), .Clk(Clk), .Bit1(in_2[2]), .Bit2(in_2[1]), .Bit3(in_2[0]), .Addr(1'b1), .out_7(out_3[3]),
    .out_8(out_3[2]), .out_9(out_3[1]), .out_10(out_3[0]));
endmodule

module RegisterBlock (
  input  Clk,
  input  [3:0] in_2,
  input  ReadReg1,
  input  Addr,
  input  WriteReg,
  input  ReadReg2,
  output [3:0] R1,
  output [3:0] R2
);

  wire and_1_out, and_2_out, and_3_out, and_4_out, not_1_out, rbnibble_1_out_7, rbnibble_1_out_8,
       rbnibble_1_out_9, rbnibble_1_out_10, rbnibble_2_out_7, rbnibble_2_out_8, rbnibble_2_out_9,
       rbnibble_2_out_10;

  and and_1 (and_1_out, WriteReg, in_2[3]);
  and and_2 (and_2_out, WriteReg, in_2[2]);
  and and_3 (and_3_out, WriteReg, in_2[1]);
  and and_4 (and_4_out, WriteReg, in_2[0]);
  not not_1 (not_1_out, Addr);
  RBNibble rbnibble_1 (
    .Bit0(and_1_out), .Clk(Clk), .Bit1(and_2_out), .Bit2(and_3_out), .Bit3(and_4_out), .Addr(not_1_out),
    .out_7(rbnibble_1_out_7), .out_8(rbnibble_1_out_8), .out_9(rbnibble_1_out_9), .out_10(rbnibble_1_out_10));
  RBNibble rbnibble_2 (
    .Bit0(and_1_out), .Clk(Clk), .Bit1(and_2_out), .Bit2(and_3_out), .Bit3(and_4_out), .Addr(Addr),
    .out_7(rbnibble_2_out_7), .out_8(rbnibble_2_out_8), .out_9(rbnibble_2_out_9), .out_10(rbnibble_2_out_10));
  and and_5 (R1[3], rbnibble_1_out_7, ReadReg1);
  and and_6 (R1[2], rbnibble_1_out_8, ReadReg1);
  and and_7 (R1[1], rbnibble_1_out_9, ReadReg1);
  and and_8 (R1[0], rbnibble_1_out_10, ReadReg1);
  and and_9 (R2[3], rbnibble_2_out_7, ReadReg2);
  and and_10 (R2[2], rbnibble_2_out_8, ReadReg2);
  and and_11 (R2[1], rbnibble_2_out_9, ReadReg2);
  and and_12 (R2[0], rbnibble_2_out_10, ReadReg2);
endmodule

module DataRAM (
  input  Clk,
  input  [3:0] in_2,
  input  Addr,
  input  Mode,
  output [3:0] out_5
);

  wire and_1_out, and_2_out, and_3_out, and_4_out, and_5_out, and_6_out, and_7_out, and_8_out, and_9_out,
       and_10_out, and_11_out, and_12_out, nibble_1_out_7, nibble_1_out_8, nibble_1_out_9, nibble_1_out_10,
       nibble_2_out_7, nibble_2_out_8, nibble_2_out_9, nibble_2_out_10, not_1_out, not_2_out;

  not not_1 (not_1_out, Mode);
  and and_1 (and_1_out, not_1_out, in_2[3]);
  and and_2 (and_2_out, not_1_out, in_2[2]);
  and and_3 (and_3_out, not_1_out, in_2[1]);
  and and_4 (and_4_out, not_1_out, in_2[0]);
  not not_2 (not_2_out, Addr);
  Nibble nibble_1 (
    .Bit0(and_1_out), .Clk(Clk), .Bit1(and_2_out), .Bit2(and_3_out), .Bit3(and_4_out), .Addr(not_2_out),
    .out_7(nibble_1_out_7), .out_8(nibble_1_out_8), .out_9(nibble_1_out_9), .out_10(nibble_1_out_10));
  Nibble nibble_2 (
    .Bit0(and_1_out), .Clk(Clk), .Bit1(and_2_out), .Bit2(and_3_out), .Bit3(and_4_out), .Addr(Addr),
    .out_7(nibble_2_out_7), .out_8(nibble_2_out_8), .out_9(nibble_2_out_9), .out_10(nibble_2_out_10));
  and and_5 (and_5_out, nibble_1_out_7, Mode);
  and and_6 (and_6_out, nibble_1_out_8, Mode);
  buf and_7 (and_7_out, nibble_1_out_9);  // AND_Gate
  and and_8 (and_8_out, nibble_1_out_10, Mode);
  and and_9 (and_9_out, nibble_2_out_7, Mode);
  and and_10 (and_10_out, nibble_2_out_8, Mode);
  and and_11 (and_11_out, nibble_2_out_9, Mode);
  and and_12 (and_12_out, nibble_2_out_10, Mode);
  or or_1 (out_5[3], and_5_out, and_9_out);
  or or_2 (out_5[2], and_6_out, and_10_out);
  or or_3 (out_5[1], and_7_out, and_11_out);
  or or_4 (out_5[0], and_8_out, and_12_out);
endmodule

module Nibble (
  input  Bit0,
  input  Clk,
  input  Bit1,
  input  Bit2,
  input  Bit3,
  input  Addr,
  output out_7,
  output out_8,
  output out_9,
  output out_10
);

  wire and_1_out, and_2_out, and_3_out, and_4_out, d_ff_1_q, d_ff_2_q, d_ff_3_q, d_ff_4_q;

  D_Flip_Flop d_ff_1 (.D(Bit0), .clk(and_1_out), .Q(d_ff_1_q));  // open: Qn, preset, reset
  and and_1 (and_1_out, Addr, Clk);
  D_Flip_Flop d_ff_2 (.D(Bit1), .clk(and_2_out), .Q(d_ff_2_q));  // open: Qn, preset, reset
  and and_2 (and_2_out, Addr, Clk);
  D_Flip_Flop d_ff_3 (.D(Bit2), .clk(and_3_out), .Q(d_ff_3_q));  // open: Qn, preset, reset
  and and_3 (and_3_out, Addr, Clk);
  D_Flip_Flop d_ff_4 (.D(Bit3), .clk(and_4_out), .Q(d_ff_4_q));  // open: Qn, preset, reset
  and and_4 (and_4_out, Addr, Clk);
  and and_5 (out_7, d_ff_1_q, Addr);
  and and_6 (out_8, d_ff_2_q, Addr);
  and and_7 (out_9, d_ff_3_q, Addr);
  and and_8 (out_10, d_ff_4_q, Addr);
endmodule

module IRNibble (
  input  Bit0,
  input  Bit1,
  input  Bit2,
  input  Bit3,
  input  Addr,
  input  Clk,
  output out_7,
  output out_8,
  output out_9,
  output out_10
);

  wire d_ff_1_q, d_ff_2_q, d_ff_3_q, d_ff_4_q, undriven;

  D_Flip_Flop #(.trigger("high")) d_ff_1 (.D(Bit0), .Q(d_ff_1_q));  // open: clk, Qn, preset, reset
  // AND_Gate and_1 has open pins: in0=Addr, in1=undriven, out=open
  D_Flip_Flop #(.trigger("low")) d_ff_2 (.D(Bit1), .Q(d_ff_2_q));  // open: clk, Qn, preset, reset
  // AND_Gate and_2 has open pins: in0=Addr, in1=undriven, out=open
  D_Flip_Flop #(.trigger("low")) d_ff_3 (.D(Bit2), .Q(d_ff_3_q));  // open: clk, Qn, preset, reset
  // AND_Gate and_3 has open pins: in0=Addr, in1=undriven, out=open
  D_Flip_Flop #(.trigger("low")) d_ff_4 (.D(Bit3), .Q(d_ff_4_q));  // open: clk, Qn, preset, reset
  // AND_Gate and_4 has open pins: in0=Addr, in1=undriven, out=open
  and and_5 (out_7, d_ff_1_q, Addr);
  and and_6 (out_8, d_ff_2_q, Addr);
  and and_7 (out_9, d_ff_3_q, Addr);
  and and_8 (out_10, d_ff_4_q, Addr);
endmodule

module RBNibble (
  input  Bit0,
  input  Clk,
  input  Bit1,
  input  Bit2,
  input  Bit3,
  input  Addr,
  output out_7,
  output out_8,
  output out_9,
  output out_10
);

  wire and_1_out, and_2_out, and_3_out, and_4_out, d_ff_1_q, d_ff_2_q, d_ff_3_q, d_ff_4_q;

  D_Flip_Flop d_ff_1 (.D(Bit0), .clk(and_1_out), .Q(d_ff_1_q));  // open: Qn, preset, reset
  and and_1 (and_1_out, Addr, Clk);
  D_Flip_Flop d_ff_2 (.D(Bit1), .clk(and_2_out), .Q(d_ff_2_q));  // open: Qn, preset, reset
  and and_2 (and_2_out, Addr, Clk);
  D_Flip_Flop d_ff_3 (.D(Bit2), .clk(and_3_out), .Q(d_ff_3_q));  // open: Qn, preset, reset
  and and_3 (and_3_out, Addr, Clk);
  D_Flip_Flop d_ff_4 (.D(Bit3), .clk(and_4_out), .Q(d_ff_4_q));  // open: Qn, preset, reset
  and and_4 (and_4_out, Addr, Clk);
  buf and_5 (out_7, d_ff_1_q);  // AND_Gate
  buf and_6 (out_8, d_ff_2_q);  // AND_Gate
  buf and_7 (out_9, d_ff_3_q);  // AND_Gate
  buf and_8 (out_10, d_ff_4_q);  // AND_Gate
endmodule
